// Logisim project Circuito Abyss.circ as structural Verilog: 6 circuits, main circuit main
module main (
  input  T,
  input  [3:0] Input_A,
  input  [3:0] Input_B,
  output Overflow
);

  wire Cond_T_2_o, Cond_T_3_o, Cond_T_4_o, Cond_T_o, \Función_2_fx , \Función_2_gx , \Función_fx ,
       \Función_gx , hexadecimal_1_a, hexadecimal_1_b, hexadecimal_1_c, hexadecimal_1_d, hexadecimal_1_e,
       hexadecimal_1_f, hexadecimal_1_g, Suma_Bin_o0, Suma_Bin_o1, Suma_Bin_o2, Suma_Bin_o3;

  Suma_en_bits_separados Suma_Bin (
    .A(Input_A), .B(Input_B), .O0(Suma_Bin_o0), .O1(Suma_Bin_o1), .O2(Suma_Bin_o2), .O3(Suma_Bin_o3),
    .Overflow(Overflow));
  \Función_cuando_w_es_1_o_0  \Función  (.Input(Input_A), .gx(\Función_gx ), .fx(\Función_fx ));
  \Función_cuando_w_es_1_o_0  \Función_2  (.Input(Input_B), .gx(\Función_2_gx ), .fx(\Función_2_fx ));
  \Condición1  Cond_T (.T(T), .F1(Suma_Bin_o0), .F2(\Función_fx ), .O(Cond_T_o));
  \Condición1  Cond_T_2 (.T(T), .F1(Suma_Bin_o1), .F2(\Función_gx ), .O(Cond_T_2_o));
  \Condición1  Cond_T_3 (.T(T), .F1(Suma_Bin_o2), .F2(\Función_2_fx ), .O(Cond_T_3_o));
  \Condición1  Cond_T_4 (.T(T), .F1(Suma_Bin_o3), .F2(\Función_2_gx ), .O(Cond_T_4_o));
  Hexadecimal hexadecimal_1 (
    .Bit1(Cond_T_o), .Bit2(Cond_T_2_o), .Bit3(Cond_T_3_o), .Bit4(Cond_T_4_o), .a(hexadecimal_1_a),
    .b(hexadecimal_1_b), .c(hexadecimal_1_c), .d(hexadecimal_1_d), .e(hexadecimal_1_e), .f(hexadecimal_1_f),
    .g(hexadecimal_1_g));
  LED led_1 (.in(hexadecimal_1_a));
  LED led_2 (.in(hexadecimal_1_a));
  LED led_3 (.in(hexadecimal_1_b));
  LED led_4 (.in(hexadecimal_1_b));
  LED led_5 (.in(hexadecimal_1_b));
  LED led_6 (.in(hexadecimal_1_g));
  LED led_7 (.in(hexadecimal_1_g));
  LED led_8 (.in(hexadecimal_1_c));
  LED led_9 (.in(hexadecimal_1_c));
  LED led_10 (.in(hexadecimal_1_c));
  LED led_11 (.in(hexadecimal_1_d));
  LED led_12 (.in(hexadecimal_1_a));
  LED led_13 (.in(hexadecimal_1_f));
  LED led_14 (.in(hexadecimal_1_f));
  LED led_15 (.in(hexadecimal_1_f));
  LED led_16 (.in(hexadecimal_1_g));
  LED led_17 (.in(hexadecimal_1_e));
  LED led_18 (.in(hexadecimal_1_e));
  LED led_19 (.in(hexadecimal_1_e));
  LED led_20 (.in(hexadecimal_1_d));
  LED led_21 (.in(hexadecimal_1_d));
endmodule

module \Condición1  (
  input  T,
  input  F1,
  input  F2,
  output O
);

  wire and_1_out, and_2_out, not_1_out;

  not not_1 (not_1_out, T);
  and and_1 (and_1_out, not_1_out, F1);
  and and_2 (and_2_out, T, F2);
  or or_1 (O, and_1_out, and_2_out);

  // Notes on the sheet:
  //   Si T=0, pasa a suma binaria
  //   Si T=1, se usa la f(x) o g(x)
  //   F1 es la suma binaria
  //   F2 es la función f(x) o g(x) (respectivamente)
endmodule

module Ayuda_para_la_suma (
  input  Carry,
  input  A,
  input  B,
  output Suma,
  output Carry_salida
);

  wire and_1_out, and_2_out, xor_1_out;

  xor xor_1 (xor_1_out, A, B);
  xor xor_2 (Suma, xor_1_out, Carry);
  and and_1 (and_1_out, Carry, xor_1_out);
  and and_2 (and_2_out, B, A);
  xor xor_3 (Carry_salida, and_1_out, and_2_out);
endmodule

module Suma_en_bits_separados (
  input  [3:0] A,
  input  [3:0] B,
  output O0,
  output O1,
  output O2,
  output O3,
  output Overflow
);

  wire ayuda_para_la_suma_1_carry_salida, ayuda_para_la_suma_2_carry_salida,
       ayuda_para_la_suma_3_carry_salida;

  Ayuda_para_la_suma ayuda_para_la_suma_1 (
    .Carry(1'b0), .A(A[0]), .B(B[0]), .Suma(O3), .Carry_salida(ayuda_para_la_suma_1_carry_salida));
  Ayuda_para_la_suma ayuda_para_la_suma_2 (
    .Carry(ayuda_para_la_suma_1_carry_salida), .A(A[1]), .B(B[1]), .Suma(O2),
    .Carry_salida(ayuda_para_la_suma_2_carry_salida));
  Ayuda_para_la_suma ayuda_para_la_suma_3 (
    .Carry(ayuda_para_la_suma_2_carry_salida), .A(A[2]), .B(B[2]), .Suma(O1),
    .Carry_salida(ayuda_para_la_suma_3_carry_salida));
  Ayuda_para_la_suma ayuda_para_la_suma_4 (
    .Carry(ayuda_para_la_suma_3_carry_salida), .A(A[3]), .B(B[3]), .Suma(O0), .Carry_salida(Overflow));

  // Notes on the sheet:
  //   Bit menos significativo
  //   Bit más significativo
endmodule

module \Función_cuando_w_es_1_o_0  (
  input  [3:0] Input,
  output gx,
  output fx
);

  wire and_1_out, and_2_out, and_3_out, and_4_out, nor_1_out, not_1_out, not_2_out, not_3_out, not_4_out,
       not_5_out, not_6_out, or_1_out;

  not not_1 (not_1_out, Input[2]);
  not not_2 (not_2_out, Input[1]);
  not not_3 (not_3_out, Input[1]);
  not not_4 (not_4_out, Input[0]);
  not not_5 (not_5_out, Input[2]);
  not not_6 (not_6_out, Input[0]);
  and and_1 (and_1_out, Input[2], Input[1], Input[0]);
  and and_2 (and_2_out, not_1_out, not_2_out);
  and and_3 (and_3_out, not_3_out, not_4_out);
  and and_4 (and_4_out, not_5_out, not_6_out);
  or or_1 (or_1_out, and_1_out, and_2_out, and_3_out, and_4_out);
  nor nor_1 (nor_1_out, Input[2], Input[1], Input[0]);
  xor xor_1 (fx, or_1_out, nor_1_out);
  xor xor_2 (gx, Input[3], fx);
endmodule

module Hexadecimal (
  input  Bit1,
  input  Bit2,
  input  Bit3,
  input  Bit4,
  output a,
  output b,
  output c,
  output d,
  output e,
  output f,
  output g
);

  wire and_1_out, and_2_out, and_3_out, and_4_out, and_5_out, and_6_out, and_7_out, and_8_out, and_9_out,
       and_10_out, and_11_out, and_12_out, and_13_out, and_14_out, and_15_out, and_16_out, and_17_out,
       and_18_out, and_19_out, and_20_out, and_21_out, and_22_out, and_23_out, and_24_out, and_25_out,
       and_26_out, and_27_out, and_28_out, and_29_out, and_30_out, and_31_out, and_32_out, and_33_out,
       and_34_out, and_35_out, not_1_out, not_2_out, not_3_out, not_4_out, not_5_out, not_6_out, not_7_out,
       not_8_out, not_9_out, not_10_out, not_11_out, not_12_out, not_13_out, not_14_out, not_15_out,
       not_16_out, not_17_out, not_18_out, not_19_out, not_20_out, not_21_out, not_22_out, not_23_out,
       not_24_out, not_25_out, not_26_out, not_27_out, not_28_out, not_29_out, not_30_out, not_31_out,
       not_32_out, not_33_out, not_34_out, not_35_out, not_36_out, not_37_out, not_38_out, not_39_out,
       not_40_out, not_41_out, not_42_out, not_43_out, not_44_out;

  not not_1 (not_1_out, Bit2);
  and and_1 (and_1_out, not_1_out, not_2_out);
  not not_2 (not_2_out, Bit4);
  not not_3 (not_3_out, Bit1);
  and and_2 (and_2_out, not_3_out, Bit3);
  not not_4 (not_4_out, Bit1);
  and and_3 (and_3_out, not_4_out, Bit2, Bit4);
  and and_4 (and_4_out, Bit2, Bit3);
  not not_5 (not_5_out, Bit2);
  and and_5 (and_5_out, Bit1, not_5_out, not_6_out);
  not not_6 (not_6_out, Bit3);
  and and_6 (and_6_out, Bit1, not_7_out);
  not not_7 (not_7_out, Bit4);
  not not_8 (not_8_out, Bit3);
  and and_7 (and_7_out, not_8_out, not_9_out);
  not not_9 (not_9_out, Bit4);
  not not_10 (not_10_out, Bit1);
  and and_8 (and_8_out, not_10_out, Bit2, not_11_out);
  not not_11 (not_11_out, Bit3);
  and and_9 (and_9_out, Bit2, not_12_out);
  not not_12 (not_12_out, Bit4);
  and and_10 (and_10_out, Bit1, not_13_out);
  not not_13 (not_13_out, Bit2);
  and and_11 (and_11_out, Bit1, Bit3);
  not not_14 (not_14_out, Bit2);
  and and_12 (and_12_out, not_14_out, not_15_out);
  not not_15 (not_15_out, Bit4);
  and and_13 (and_13_out, Bit3, not_16_out);
  not not_16 (not_16_out, Bit4);
  and and_14 (and_14_out, Bit1, Bit3);
  and and_15 (and_15_out, Bit1, Bit2);
  not not_17 (not_17_out, Bit1);
  not not_18 (not_18_out, Bit2);
  and and_16 (and_16_out, not_17_out, not_18_out, not_19_out);
  not not_19 (not_19_out, Bit4);
  not not_20 (not_20_out, Bit2);
  and and_17 (and_17_out, not_20_out, Bit3, Bit4);
  and and_18 (and_18_out, Bit2, not_21_out, Bit4);
  not not_21 (not_21_out, Bit3);
  and and_19 (and_19_out, Bit2, Bit3, not_22_out);
  not not_22 (not_22_out, Bit4);
  and and_20 (and_20_out, Bit1, not_23_out, not_24_out);
  not not_23 (not_23_out, Bit3);
  not not_24 (not_24_out, Bit4);
  not not_25 (not_25_out, Bit1);
  and and_21 (and_21_out, not_25_out, not_26_out);
  not not_26 (not_26_out, Bit3);
  not not_27 (not_27_out, Bit1);
  and and_22 (and_22_out, not_27_out, Bit4);
  not not_28 (not_28_out, Bit3);
  and and_23 (and_23_out, not_28_out, Bit4);
  not not_29 (not_29_out, Bit1);
  and and_24 (and_24_out, not_29_out, Bit2);
  and and_25 (and_25_out, Bit1, not_30_out);
  not not_30 (not_30_out, Bit2);
  not not_31 (not_31_out, Bit1);
  and and_26 (and_26_out, not_31_out, not_32_out);
  not not_32 (not_32_out, Bit2);
  not not_33 (not_33_out, Bit1);
  and and_27 (and_27_out, not_33_out, not_34_out, not_35_out);
  not not_34 (not_34_out, Bit3);
  not not_35 (not_35_out, Bit4);
  not not_36 (not_36_out, Bit2);
  and and_28 (and_28_out, not_36_out, not_37_out);
  not not_37 (not_37_out, Bit4);
  not not_38 (not_38_out, Bit1);
  and and_29 (and_29_out, not_38_out, Bit3, Bit4);
  not not_39 (not_39_out, Bit3);
  and and_30 (and_30_out, Bit1, not_39_out, Bit4);
  not not_40 (not_40_out, Bit2);
  and and_31 (and_31_out, not_40_out, Bit3);
  and and_32 (and_32_out, Bit3, not_41_out);
  not not_41 (not_41_out, Bit4);
  not not_42 (not_42_out, Bit1);
  and and_33 (and_33_out, not_42_out, Bit2, not_43_out);
  not not_43 (not_43_out, Bit3);
  and and_34 (and_34_out, Bit1, not_44_out);
  not not_44 (not_44_out, Bit2);
  and and_35 (and_35_out, Bit1, Bit4);
  or or_1 (b, and_7_out, and_8_out, and_9_out, and_10_out, and_11_out);
  or or_2 (c, and_12_out, and_13_out, and_14_out, and_15_out);
  or or_3 (d, and_16_out, and_17_out, and_18_out, and_19_out, and_20_out);
  or or_4 (e, and_21_out, and_22_out, and_23_out, and_24_out, and_25_out);
  or or_5 (f, and_26_out, and_27_out, and_28_out, and_29_out, and_30_out);
  or or_6 (g, and_31_out, and_32_out, and_33_out, and_34_out, and_35_out);
  or or_7 (a, and_1_out, and_2_out, and_3_out, and_4_out, and_5_out, and_6_out);

  // Notes on the sheet:
  //   Se crea la tabla de verdad y se forma el circuito respectivo
endmodule
