// Logisim project Tarea3.circ as structural Verilog: 9 circuits, main circuit main
module main (
  input  [1:0] M,
  input  [7:0] X
);

  wire clock_1_out, not_1_out;
  wire [7:0] ff1_1_out_3, ff2_1_out_3, s_logic_1_s;

  Clock clock_1 (.out(clock_1_out));
  FF1 ff1_1 (.X(X), .CLK(clock_1_out), .out_3(ff1_1_out_3));
  not not_1 (not_1_out, clock_1_out);
  S_Logic s_logic_1 (.P_X(ff2_1_out_3), .X(ff1_1_out_3), .M(M), .S(s_logic_1_s));
  FF2 ff2_1 (.X(ff1_1_out_3), .CLK(not_1_out), .out_3(ff2_1_out_3));
  LED s7 (.in(s_logic_1_s[7]));
  LED s6 (.in(s_logic_1_s[6]));
  LED s5 (.in(s_logic_1_s[5]));
  LED s4 (.in(s_logic_1_s[4]));
  LED s1 (.in(s_logic_1_s[1]));
  LED s2 (.in(s_logic_1_s[2]));
  LED s0 (.in(s_logic_1_s[0]));
  LED s3 (.in(s_logic_1_s[3]));
endmodule

module FF1 (
  input  CLK,
  input  [7:0] X,
  output [7:0] out_3
);

  Auxiliar auxiliar_1 (.D(X[7]), .CLK(CLK), .Q(out_3[7]));
  Auxiliar auxiliar_2 (.D(X[6]), .CLK(CLK), .Q(out_3[6]));
  Auxiliar auxiliar_3 (.D(X[5]), .CLK(CLK), .Q(out_3[5]));
  Auxiliar auxiliar_4 (.D(X[4]), .CLK(CLK), .Q(out_3[4]));
  Auxiliar auxiliar_5 (.D(X[3]), .CLK(CLK), .Q(out_3[3]));
  Auxiliar auxiliar_6 (.D(X[2]), .CLK(CLK), .Q(out_3[2]));
  Auxiliar auxiliar_7 (.D(X[1]), .CLK(CLK), .Q(out_3[1]));
  Auxiliar auxiliar_8 (.D(X[0]), .CLK(CLK), .Q(out_3[0]));
endmodule

module FF2 (
  input  CLK,
  input  [7:0] X,
  output [7:0] out_3
);

  Auxiliar auxiliar_1 (.D(X[7]), .CLK(CLK), .Q(out_3[7]));
  Auxiliar auxiliar_2 (.D(X[6]), .CLK(CLK), .Q(out_3[6]));
  Auxiliar auxiliar_3 (.D(X[5]), .CLK(CLK), .Q(out_3[5]));
  Auxiliar auxiliar_4 (.D(X[4]), .CLK(CLK), .Q(out_3[4]));
  Auxiliar auxiliar_5 (.D(X[3]), .CLK(CLK), .Q(out_3[3]));
  Auxiliar auxiliar_6 (.D(X[2]), .CLK(CLK), .Q(out_3[2]));
  Auxiliar auxiliar_7 (.D(X[1]), .CLK(CLK), .Q(out_3[1]));
  Auxiliar auxiliar_8 (.D(X[0]), .CLK(CLK), .Q(out_3[0]));
endmodule

// Aux
module Auxiliar (
  input  CLK,
  input  D,
  output Q
);

  wire and_1_out, and_2_out, not_1_out;

  not not_1 (not_1_out, D);
  and and_1 (and_1_out, not_1_out, CLK);
  and and_2 (and_2_out, CLK, D);
  SR sr_1 (.R(and_1_out), .S(and_2_out), .Q(Q));
endmodule

module SR (
  input  R,
  input  S,
  output Q
);

  wire nor_2_out;

  nor nor_1 (Q, R, nor_2_out);
  nor nor_2 (nor_2_out, Q, S);
endmodule

module S_Logic (
  input  [1:0] M,
  input  [7:0] P_X,
  input  [7:0] X,
  output [7:0] S
);

  wire [7:0] AND_out, OR_out, resta_1_out_3, sumbinary_1_out_4;

  SumBinary sumbinary_1 (.in_1(1'b0), .P_X(P_X), .X(X), .out_4(sumbinary_1_out_4));
  Resta resta_1 (.X(X), .P_X(P_X), .out_3(resta_1_out_3));
  assign OR_out = P_X | X;  // OR_Gate OR, 8 bits wide
  assign AND_out = P_X & X;  // AND_Gate AND, 8 bits wide
  Multiplexer #(.select(2), .width(8)) multiplexer_1 (
    .in0(sumbinary_1_out_4), .in1(resta_1_out_3), .in2(OR_out), .in3(AND_out), .out(S), .sel(M), .en(1'b1));
endmodule

module AuxSum (
  input  Carry,
  input  A,
  input  B,
  output Suma,
  output Carry_salida
);

  wire and_1_out, and_2_out, xor_1_out;

  xor xor_1 (xor_1_out, A, B);
  xor xor_2 (Suma, xor_1_out, Carry);
  and and_1 (and_1_out, Carry, xor_1_out);
  and and_2 (and_2_out, B, A);
  xor xor_3 (Carry_salida, and_1_out, and_2_out);
endmodule

// SUM
module SumBinary (
  input  in_1,
  input  [7:0] P_X,
  input  [7:0] X,
  output [7:0] out_4
);

  wire auxsum_1_carry_salida, auxsum_2_carry_salida, auxsum_3_carry_salida, auxsum_4_carry_salida,
       auxsum_5_carry_salida, auxsum_6_carry_salida, auxsum_7_carry_salida, auxsum_8_carry_salida;

  AuxSum auxsum_1 (.Carry(in_1), .A(P_X[0]), .B(X[0]), .Suma(out_4[0]), .Carry_salida(auxsum_1_carry_salida));
  AuxSum auxsum_2 (
    .Carry(auxsum_1_carry_salida), .A(P_X[1]), .B(X[1]), .Suma(out_4[1]), .Carry_salida(auxsum_2_carry_salida));
  AuxSum auxsum_3 (
    .Carry(auxsum_2_carry_salida), .A(P_X[2]), .B(X[2]), .Suma(out_4[2]), .Carry_salida(auxsum_3_carry_salida));
  AuxSum auxsum_4 (
    .Carry(auxsum_3_carry_salida), .A(P_X[3]), .B(X[3]), .Suma(out_4[3]), .Carry_salida(auxsum_4_carry_salida));
  AuxSum auxsum_5 (
    .Carry(auxsum_4_carry_salida), .A(P_X[4]), .B(X[4]), .Suma(out_4[4]), .Carry_salida(auxsum_5_carry_salida));
  AuxSum auxsum_6 (
    .Carry(auxsum_5_carry_salida), .A(P_X[5]), .B(X[5]), .Suma(out_4[5]), .Carry_salida(auxsum_6_carry_salida));
  AuxSum auxsum_7 (
    .Carry(auxsum_6_carry_salida), .A(P_X[6]), .B(X[6]), .Suma(out_4[6]), .Carry_salida(auxsum_7_carry_salida));
  AuxSum auxsum_8 (
    .Carry(auxsum_7_carry_salida), .A(P_X[7]), .B(X[7]), .Suma(out_4[7]), .Carry_salida(auxsum_8_carry_salida));
  // Probe on auxsum_8_carry_salida

  // Notes on the sheet:
  //   Bit menos significativo
  //   Bit mas significativo
endmodule

module Resta (
  input  [7:0] X,
  input  [7:0] P_X,
  output [7:0] out_3
);

  wire [7:0] not_1_out;

  assign not_1_out = ~P_X;  // NOT_Gate not_1, 8 bits wide
  SumBinary sumbinary_1 (.in_1(1'b1), .P_X(X), .X(not_1_out), .out_4(out_3));
endmodule
